// Logisim project LabSession10.circ as structural Verilog: 4 circuits, main circuit main
module main (
  output [31:0] out_1
);

  wire Clk_out;
  wire [31:0] instruction_fetch_1_ir;

  Clock Clk (.out(Clk_out));
  Instruction_Fetch instruction_fetch_1 (.Clk(Clk_out), .En(1'b1), .IR(instruction_fetch_1_ir));
  Hex_Digit_Display hex_digit_display_1 (.value(out_1[31:28]));  // open: dp
  ALU alu_1 (.ALUOperation(3'b000), .SRC1(32'h12), .SRC2(32'ha), .ALUResult(out_1));
  Register #(.width(32)) IR (.D(instruction_fetch_1_ir), .clk(Clk_out));  // open: en, Q, clr
  Hex_Digit_Display hex_digit_display_2 (.value(out_1[27:24]));  // open: dp
  Hex_Digit_Display hex_digit_display_3 (.value(out_1[23:20]));  // open: dp
  Hex_Digit_Display hex_digit_display_4 (.value(out_1[19:16]));  // open: dp
  Hex_Digit_Display hex_digit_display_5 (.value(out_1[15:12]));  // open: dp
  Hex_Digit_Display hex_digit_display_6 (.value(out_1[7:4]));  // open: dp
  Hex_Digit_Display hex_digit_display_7 (.value(out_1[11:8]));  // open: dp
  Hex_Digit_Display hex_digit_display_8 (.value(out_1[3:0]));  // open: dp

  // Notes on the sheet:
  //   Enable
endmodule

module RegFile32 (
  input  in_1,
  input  [4:0] in_2
);

  wire and_1_out, and_2_out, and_3_out, and_4_out, and_5_out, and_6_out, and_7_out, and_8_out, and_9_out,
       and_10_out, and_11_out, and_12_out, and_13_out, and_14_out, and_15_out, and_16_out, and_17_out,
       and_18_out, and_19_out, and_20_out, and_21_out, and_22_out, and_23_out, and_24_out, and_25_out,
       and_26_out, and_27_out, and_28_out, and_29_out, and_30_out, and_31_out, and_32_out, decoder_1_out0,
       decoder_1_out1, decoder_1_out2, decoder_1_out3, decoder_1_out4, decoder_1_out5, decoder_1_out6,
       decoder_1_out7, decoder_1_out8, decoder_1_out9, decoder_1_out10, decoder_1_out11, decoder_1_out12,
       decoder_1_out13, decoder_1_out14, decoder_1_out15, decoder_1_out16, decoder_1_out17, decoder_1_out18,
       decoder_1_out19, decoder_1_out20, decoder_1_out21, decoder_1_out22, decoder_1_out23, decoder_1_out24,
       decoder_1_out25, decoder_1_out26, decoder_1_out27, decoder_1_out28, decoder_1_out29, decoder_1_out30,
       decoder_1_out31;

  Decoder #(.select(5), .enable("false")) decoder_1 (
    .out0(decoder_1_out0), .out1(decoder_1_out1), .out2(decoder_1_out2), .out3(decoder_1_out3),
    .out4(decoder_1_out4), .out5(decoder_1_out5), .out6(decoder_1_out6), .out7(decoder_1_out7),
    .out8(decoder_1_out8), .out9(decoder_1_out9), .out10(decoder_1_out10), .out11(decoder_1_out11),
    .out12(decoder_1_out12), .out13(decoder_1_out13), .out14(decoder_1_out14), .out15(decoder_1_out15),
    .out16(decoder_1_out16), .out17(decoder_1_out17), .out18(decoder_1_out18), .out19(decoder_1_out19),
    .out20(decoder_1_out20), .out21(decoder_1_out21), .out22(decoder_1_out22), .out23(decoder_1_out23),
    .out24(decoder_1_out24), .out25(decoder_1_out25), .out26(decoder_1_out26), .out27(decoder_1_out27),
    .out28(decoder_1_out28), .out29(decoder_1_out29), .out30(decoder_1_out30), .out31(decoder_1_out31),
    .sel(in_2));
  Register #(.width(32)) register_1 (.en(and_1_out), .clk(in_1));  // open: D, Q, clr
  buf and_1 (and_1_out, decoder_1_out0);  // AND_Gate
  Register #(.width(32)) register_2 (.en(and_2_out), .clk(in_1));  // open: D, Q, clr
  buf and_2 (and_2_out, decoder_1_out4);  // AND_Gate
  Register #(.width(32)) register_3 (.en(and_3_out), .clk(in_1));  // open: D, Q, clr
  buf and_3 (and_3_out, decoder_1_out8);  // AND_Gate
  Register #(.width(32)) register_4 (.en(and_4_out), .clk(in_1));  // open: D, Q, clr
  buf and_4 (and_4_out, decoder_1_out12);  // AND_Gate
  Register #(.width(32)) register_5 (.en(and_5_out), .clk(in_1));  // open: D, Q, clr
  buf and_5 (and_5_out, decoder_1_out16);  // AND_Gate
  Register #(.width(32)) register_6 (.en(and_6_out), .clk(in_1));  // open: D, Q, clr
  buf and_6 (and_6_out, decoder_1_out20);  // AND_Gate
  Register #(.width(32)) register_7 (.en(and_7_out), .clk(in_1));  // open: D, Q, clr
  buf and_7 (and_7_out, decoder_1_out24);  // AND_Gate
  Register #(.width(32)) register_8 (.en(and_8_out), .clk(in_1));  // open: D, Q, clr
  buf and_8 (and_8_out, decoder_1_out28);  // AND_Gate
  buf and_9 (and_9_out, decoder_1_out1);  // AND_Gate
  buf and_10 (and_10_out, decoder_1_out5);  // AND_Gate
  buf and_11 (and_11_out, decoder_1_out9);  // AND_Gate
  buf and_12 (and_12_out, decoder_1_out13);  // AND_Gate
  buf and_13 (and_13_out, decoder_1_out17);  // AND_Gate
  buf and_14 (and_14_out, decoder_1_out21);  // AND_Gate
  buf and_15 (and_15_out, decoder_1_out25);  // AND_Gate
  buf and_16 (and_16_out, decoder_1_out29);  // AND_Gate
  Register #(.width(32)) register_9 (.en(and_9_out));  // open: D, Q, clk, clr
  Register #(.width(32)) register_10 (.en(and_10_out));  // open: D, Q, clk, clr
  Register #(.width(32)) register_11 (.en(and_11_out));  // open: D, Q, clk, clr
  Register #(.width(32)) register_12 (.en(and_12_out));  // open: D, Q, clk, clr
  Register #(.width(32)) register_13 (.en(and_13_out));  // open: D, Q, clk, clr
  Register #(.width(32)) register_14 (.en(and_14_out));  // open: D, Q, clk, clr
  Register #(.width(32)) register_15 (.en(and_15_out));  // open: D, Q, clk, clr
  Register #(.width(32)) register_16 (.en(and_16_out));  // open: D, Q, clk, clr
  buf and_17 (and_17_out, decoder_1_out2);  // AND_Gate
  buf and_18 (and_18_out, decoder_1_out6);  // AND_Gate
  buf and_19 (and_19_out, decoder_1_out10);  // AND_Gate
  buf and_20 (and_20_out, decoder_1_out14);  // AND_Gate
  buf and_21 (and_21_out, decoder_1_out18);  // AND_Gate
  buf and_22 (and_22_out, decoder_1_out22);  // AND_Gate
  buf and_23 (and_23_out, decoder_1_out26);  // AND_Gate
  buf and_24 (and_24_out, decoder_1_out30);  // AND_Gate
  Register #(.width(32)) register_17 (.en(and_17_out));  // open: D, Q, clk, clr
  Register #(.width(32)) register_18 (.en(and_18_out));  // open: D, Q, clk, clr
  Register #(.width(32)) register_19 (.en(and_19_out));  // open: D, Q, clk, clr
  Register #(.width(32)) register_20 (.en(and_20_out));  // open: D, Q, clk, clr
  Register #(.width(32)) register_21 (.en(and_21_out));  // open: D, Q, clk, clr
  Register #(.width(32)) register_22 (.en(and_22_out));  // open: D, Q, clk, clr
  Register #(.width(32)) register_23 (.en(and_23_out));  // open: D, Q, clk, clr
  Register #(.width(32)) register_24 (.en(and_24_out));  // open: D, Q, clk, clr
  buf and_25 (and_25_out, decoder_1_out3);  // AND_Gate
  buf and_26 (and_26_out, decoder_1_out7);  // AND_Gate
  buf and_27 (and_27_out, decoder_1_out11);  // AND_Gate
  buf and_28 (and_28_out, decoder_1_out15);  // AND_Gate
  buf and_29 (and_29_out, decoder_1_out19);  // AND_Gate
  buf and_30 (and_30_out, decoder_1_out23);  // AND_Gate
  buf and_31 (and_31_out, decoder_1_out27);  // AND_Gate
  buf and_32 (and_32_out, decoder_1_out31);  // AND_Gate
  Register #(.width(32)) register_25 (.en(and_25_out));  // open: D, Q, clk, clr
  Register #(.width(32)) register_26 (.en(and_26_out));  // open: D, Q, clk, clr
  Register #(.width(32)) register_27 (.en(and_27_out));  // open: D, Q, clk, clr
  Register #(.width(32)) register_28 (.en(and_28_out));  // open: D, Q, clk, clr
  Register #(.width(32)) register_29 (.en(and_29_out));  // open: D, Q, clk, clr
  Register #(.width(32)) register_30 (.en(and_30_out));  // open: D, Q, clk, clr
  Register #(.width(32)) register_31 (.en(and_31_out));  // open: D, Q, clk, clr
  Register #(.width(32)) register_32 (.en(and_32_out));  // open: D, Q, clk, clr
  Multiplexer #(.select(5), .width(32), .enable("false")) multiplexer_1 ();  // open: in0, in1, in2, in3, in4, in5, in6, in7, in8, in9, in10, in11, in12, in13, in14, in15, in16, in17, in18, in19, in20, in21, in22, in23, in24, in25, in26, in27, in28, in29, in30, in31, out, sel
  Multiplexer #(.select(5), .width(32), .enable("false")) multiplexer_2 ();  // open: in0, in1, in2, in3, in4, in5, in6, in7, in8, in9, in10, in11, in12, in13, in14, in15, in16, in17, in18, in19, in20, in21, in22, in23, in24, in25, in26, in27, in28, in29, in30, in31, out, sel
endmodule

module Instruction_Fetch (
  input  Clk,
  input  En,
  output [31:0] IR
);

  wire [31:0] adder_1_out, PC_q;

  Register #(.width(32)) PC (.D(adder_1_out), .Q(PC_q), .clk(Clk));  // open: en, clr
  RAM #(.addrWidth(24), .dataWidth(32)) ram_1 (.addr(PC_q[23:0]), .data(IR), .clk(Clk), .ld(En));  // open: sel, clr
  Adder #(.width(32)) adder_1 (.a(PC_q), .b(32'h1), .out(adder_1_out));  // open: cin, cout
endmodule

module ALU (
  input  [2:0] ALUOperation,
  input  [31:0] SRC1,
  input  [31:0] SRC2,
  output [31:0] ALUResult
);

  wire [31:0] adder_1_out, adder_2_out, AND_out, not_1_out, OR_out;

  assign not_1_out = ~SRC2;  // NOT_Gate not_1, 32 bits wide
  assign AND_out = SRC1 & SRC2;  // AND_Gate AND, 32 bits wide
  assign OR_out = SRC1 | SRC2;  // OR_Gate OR, 32 bits wide
  Adder #(.width(32)) adder_1 (.a(SRC1), .b(SRC2), .out(adder_1_out));  // open: cin, cout
  Adder #(.width(32)) adder_2 (.a(SRC1), .b(not_1_out), .out(adder_2_out), .cin(1'b1));  // open: cout
  Multiplexer #(.select(3), .width(32), .enable("false")) multiplexer_1 (
    .in0(AND_out), .in1(OR_out), .in2(adder_1_out), .in6(adder_2_out), .out(ALUResult), .sel(ALUOperation));  // open: in3, in4, in5, in7
endmodule
