// Logisim project LabSession10.circ as structural Verilog: 8 circuits, main circuit main
module main (
  input  Write,
  output [31:0] ReadData1,
  output [31:0] ReadData2,
  output [31:0] out_4,
  output Zero_Flag
);

  wire Clk_2_out, Clk_out;
  wire [31:0] instruction_fetch_1_p3;

  Clock Clk (.out(Clk_out));
  ALU alu_1 (.ALUOperation(3'b110), .SRC1(32'h7d5), .SRC2(32'hfc7), .ZF(Zero_Flag), .ALUResult(out_4));
  RegFile32 regfile32_1 (
    .ReadReg1(5'b00011), .ReadReg2(5'b01000), .Clk(Clk_out), .Write(Write), .WriteReg(5'b00011),
    .WriteData(32'h5de6), .ReadData1(ReadData1), .ReadData2(ReadData2));
  Hex_Digit_Display hex_digit_display_1 (.value(out_4[27:24]));  // open: dp
  Hex_Digit_Display hex_digit_display_2 (.value(out_4[31:28]));  // open: dp
  Clock Clk_2 (.out(Clk_2_out));
  Hex_Digit_Display hex_digit_display_3 (.value(out_4[23:20]));  // open: dp
  Hex_Digit_Display hex_digit_display_4 (.value(out_4[19:16]));  // open: dp
  // Instruction_Fetch instruction_fetch_1: pin names not known; wires that end beside it: Clk_2_out, 1'b1, instruction_fetch_1_p3
  Hex_Digit_Display hex_digit_display_5 (.value(out_4[15:12]));  // open: dp
  Hex_Digit_Display hex_digit_display_6 (.value(out_4[11:8]));  // open: dp
  Register #(.width(32)) IR (.D(instruction_fetch_1_p3), .clk(Clk_2_out));  // open: en, Q, clr
  Hex_Digit_Display hex_digit_display_7 (.value(out_4[7:4]));  // open: dp
  Hex_Digit_Display hex_digit_display_8 (.value(out_4[3:0]));  // open: dp

  // Notes on the sheet:
  //   WriteReg
  //   WriteReg
  //   ReadReg1
  //   ReadReg2
  //   Enable
endmodule

// RegFile
module RegFile32 (
  input  [4:0] ReadReg1,
  input  [4:0] ReadReg2,
  input  Clk,
  input  Write,
  input  [4:0] WriteReg,
  input  [31:0] WriteData,
  output [31:0] ReadData1,
  output [31:0] ReadData2
);

  wire and_1_out, and_2_out, and_3_out, and_4_out, and_5_out, and_6_out, and_7_out, and_8_out, and_9_out,
       and_10_out, and_11_out, and_12_out, and_13_out, and_14_out, and_15_out, and_16_out, and_17_out,
       and_18_out, and_19_out, and_20_out, and_21_out, and_22_out, and_23_out, and_24_out, and_25_out,
       and_26_out, and_27_out, and_28_out, and_29_out, and_30_out, and_31_out, and_32_out, decoder_1_out0,
       decoder_1_out1, decoder_1_out2, decoder_1_out3, decoder_1_out4, decoder_1_out5, decoder_1_out6,
       decoder_1_out7, decoder_1_out8, decoder_1_out9, decoder_1_out10, decoder_1_out11, decoder_1_out12,
       decoder_1_out13, decoder_1_out14, decoder_1_out15, decoder_1_out16, decoder_1_out17, decoder_1_out18,
       decoder_1_out19, decoder_1_out20, decoder_1_out21, decoder_1_out22, decoder_1_out23, decoder_1_out24,
       decoder_1_out25, decoder_1_out26, decoder_1_out27, decoder_1_out28, decoder_1_out29, decoder_1_out30,
       decoder_1_out31;
  wire [31:0] register_1_q, register_2_q, register_3_q, register_4_q, register_5_q, register_6_q,
       register_7_q, register_8_q, register_9_q, register_10_q, register_11_q, register_12_q, register_13_q,
       register_14_q, register_15_q, register_16_q, register_17_q, register_18_q, register_19_q,
       register_20_q, register_21_q, register_22_q, register_23_q, register_24_q, register_25_q,
       register_26_q, register_27_q, register_28_q, register_29_q, register_30_q, register_31_q,
       register_32_q;

  Decoder #(.select(5), .enable("false")) decoder_1 (
    .out0(decoder_1_out0), .out1(decoder_1_out1), .out2(decoder_1_out2), .out3(decoder_1_out3),
    .out4(decoder_1_out4), .out5(decoder_1_out5), .out6(decoder_1_out6), .out7(decoder_1_out7),
    .out8(decoder_1_out8), .out9(decoder_1_out9), .out10(decoder_1_out10), .out11(decoder_1_out11),
    .out12(decoder_1_out12), .out13(decoder_1_out13), .out14(decoder_1_out14), .out15(decoder_1_out15),
    .out16(decoder_1_out16), .out17(decoder_1_out17), .out18(decoder_1_out18), .out19(decoder_1_out19),
    .out20(decoder_1_out20), .out21(decoder_1_out21), .out22(decoder_1_out22), .out23(decoder_1_out23),
    .out24(decoder_1_out24), .out25(decoder_1_out25), .out26(decoder_1_out26), .out27(decoder_1_out27),
    .out28(decoder_1_out28), .out29(decoder_1_out29), .out30(decoder_1_out30), .out31(decoder_1_out31),
    .sel(WriteReg));
  and and_1 (and_1_out, Write, decoder_1_out0);
  and and_2 (and_2_out, Write, decoder_1_out4);
  and and_3 (and_3_out, Write, decoder_1_out8);
  and and_4 (and_4_out, Write, decoder_1_out12);
  and and_5 (and_5_out, Write, decoder_1_out16);
  and and_6 (and_6_out, Write, decoder_1_out20);
  and and_7 (and_7_out, Write, decoder_1_out24);
  and and_8 (and_8_out, Write, decoder_1_out28);
  Register #(.width(32)) register_1 (.D(WriteData), .en(and_1_out), .Q(register_1_q), .clk(Clk));  // open: clr
  Register #(.width(32)) register_2 (.D(WriteData), .en(and_2_out), .Q(register_2_q), .clk(Clk));  // open: clr
  Register #(.width(32)) register_3 (.D(WriteData), .en(and_3_out), .Q(register_3_q), .clk(Clk));  // open: clr
  Register #(.width(32)) register_4 (.D(WriteData), .en(and_4_out), .Q(register_4_q), .clk(Clk));  // open: clr
  Register #(.width(32)) register_5 (.D(WriteData), .en(and_5_out), .Q(register_5_q), .clk(Clk));  // open: clr
  Register #(.width(32)) register_6 (.D(WriteData), .en(and_6_out), .Q(register_6_q), .clk(Clk));  // open: clr
  Register #(.width(32)) register_7 (.D(WriteData), .en(and_7_out), .Q(register_7_q), .clk(Clk));  // open: clr
  Register #(.width(32)) register_8 (.D(WriteData), .en(and_8_out), .Q(register_8_q), .clk(Clk));  // open: clr
  and and_9 (and_9_out, Write, decoder_1_out1);
  and and_10 (and_10_out, Write, decoder_1_out5);
  and and_11 (and_11_out, Write, decoder_1_out9);
  and and_12 (and_12_out, Write, decoder_1_out13);
  and and_13 (and_13_out, Write, decoder_1_out17);
  and and_14 (and_14_out, Write, decoder_1_out21);
  and and_15 (and_15_out, Write, decoder_1_out25);
  and and_16 (and_16_out, Write, decoder_1_out29);
  Register #(.width(32)) register_9 (.D(WriteData), .en(and_9_out), .Q(register_9_q), .clk(Clk));  // open: clr
  Register #(.width(32)) register_10 (.D(WriteData), .en(and_10_out), .Q(register_10_q), .clk(Clk));  // open: clr
  Register #(.width(32)) register_11 (.D(WriteData), .en(and_11_out), .Q(register_11_q), .clk(Clk));  // open: clr
  Register #(.width(32)) register_12 (.D(WriteData), .en(and_12_out), .Q(register_12_q), .clk(Clk));  // open: clr
  Register #(.width(32)) register_13 (.D(WriteData), .en(and_13_out), .Q(register_13_q), .clk(Clk));  // open: clr
  Register #(.width(32)) register_14 (.D(WriteData), .en(and_14_out), .Q(register_14_q), .clk(Clk));  // open: clr
  Register #(.width(32)) register_15 (.D(WriteData), .en(and_15_out), .Q(register_15_q), .clk(Clk));  // open: clr
  Register #(.width(32)) register_16 (.D(WriteData), .en(and_16_out), .Q(register_16_q), .clk(Clk));  // open: clr
  Register #(.width(32)) register_17 (.D(WriteData), .en(and_17_out), .Q(register_17_q), .clk(Clk));  // open: clr
  and and_17 (and_17_out, Write, decoder_1_out2);
  Register #(.width(32)) register_18 (.D(WriteData), .en(and_18_out), .Q(register_18_q), .clk(Clk));  // open: clr
  and and_18 (and_18_out, Write, decoder_1_out6);
  Register #(.width(32)) register_19 (.D(WriteData), .en(and_19_out), .Q(register_19_q), .clk(Clk));  // open: clr
  and and_19 (and_19_out, Write, decoder_1_out10);
  Register #(.width(32)) register_20 (.D(WriteData), .en(and_20_out), .Q(register_20_q), .clk(Clk));  // open: clr
  and and_20 (and_20_out, Write, decoder_1_out14);
  Register #(.width(32)) register_21 (.D(WriteData), .en(and_21_out), .Q(register_21_q), .clk(Clk));  // open: clr
  and and_21 (and_21_out, Write, decoder_1_out18);
  Register #(.width(32)) register_22 (.D(WriteData), .en(and_22_out), .Q(register_22_q), .clk(Clk));  // open: clr
  and and_22 (and_22_out, Write, decoder_1_out22);
  Register #(.width(32)) register_23 (.D(WriteData), .en(and_23_out), .Q(register_23_q), .clk(Clk));  // open: clr
  and and_23 (and_23_out, Write, decoder_1_out26);
  Register #(.width(32)) register_24 (.D(WriteData), .en(and_24_out), .Q(register_24_q), .clk(Clk));  // open: clr
  and and_24 (and_24_out, Write, decoder_1_out30);
  Register #(.width(32)) register_25 (.D(WriteData), .en(and_25_out), .Q(register_25_q), .clk(Clk));  // open: clr
  and and_25 (and_25_out, Write, decoder_1_out3);
  Register #(.width(32)) register_26 (.D(WriteData), .en(and_26_out), .Q(register_26_q), .clk(Clk));  // open: clr
  and and_26 (and_26_out, Write, decoder_1_out7);
  Register #(.width(32)) register_27 (.D(WriteData), .en(and_27_out), .Q(register_27_q), .clk(Clk));  // open: clr
  and and_27 (and_27_out, Write, decoder_1_out11);
  Register #(.width(32)) register_28 (.D(WriteData), .en(and_28_out), .Q(register_28_q), .clk(Clk));  // open: clr
  and and_28 (and_28_out, Write, decoder_1_out15);
  Register #(.width(32)) register_29 (.D(WriteData), .en(and_29_out), .Q(register_29_q), .clk(Clk));  // open: clr
  and and_29 (and_29_out, Write, decoder_1_out19);
  Register #(.width(32)) register_30 (.D(WriteData), .en(and_30_out), .Q(register_30_q), .clk(Clk));  // open: clr
  and and_30 (and_30_out, Write, decoder_1_out23);
  Register #(.width(32)) register_31 (.D(WriteData), .en(and_31_out), .Q(register_31_q), .clk(Clk));  // open: clr
  and and_31 (and_31_out, Write, decoder_1_out27);
  Register #(.width(32)) register_32 (.D(WriteData), .en(and_32_out), .Q(register_32_q), .clk(Clk));  // open: clr
  and and_32 (and_32_out, Write, decoder_1_out31);
  Multiplexer #(.select(5), .width(32), .enable("false")) multiplexer_1 (
    .in0(register_1_q), .in1(register_9_q), .in2(register_17_q), .in3(register_25_q), .in4(register_2_q),
    .in5(register_10_q), .in6(register_18_q), .in7(register_26_q), .in8(register_3_q), .in9(register_11_q),
    .in10(register_19_q), .in11(register_27_q), .in12(register_4_q), .in13(register_12_q),
    .in14(register_20_q), .in15(register_28_q), .in16(register_5_q), .in17(register_13_q),
    .in18(register_21_q), .in19(register_29_q), .in20(register_6_q), .in21(register_14_q),
    .in22(register_22_q), .in23(register_30_q), .in24(register_7_q), .in25(register_15_q),
    .in26(register_23_q), .in27(register_31_q), .in28(register_8_q), .in29(register_16_q),
    .in30(register_24_q), .in31(register_32_q), .out(ReadData1), .sel(ReadReg1));
  Multiplexer #(.select(5), .width(32), .enable("false")) multiplexer_2 (
    .in0(register_1_q), .in1(register_9_q), .in2(register_17_q), .in3(register_25_q), .in4(register_2_q),
    .in5(register_10_q), .in6(register_18_q), .in7(register_26_q), .in8(register_3_q), .in9(register_11_q),
    .in10(register_19_q), .in11(register_27_q), .in12(register_4_q), .in13(register_12_q),
    .in14(register_20_q), .in15(register_28_q), .in16(register_5_q), .in17(register_13_q),
    .in18(register_21_q), .in19(register_29_q), .in20(register_6_q), .in21(register_14_q),
    .in22(register_22_q), .in23(register_30_q), .in24(register_7_q), .in25(register_15_q),
    .in26(register_23_q), .in27(register_31_q), .in28(register_8_q), .in29(register_16_q),
    .in30(register_24_q), .in31(register_32_q), .out(ReadData2), .sel(ReadReg2));
endmodule

// IM
module Instruction_Fetch (
  input  Branch,
  input  Zero_Flag,
  input  [31:0] Immediate,
  input  Clk,
  input  En,
  output [31:0] IR
);

  wire and_1_out;
  wire [31:0] adder_1_out, adder_2_out, multiplexer_1_out, PC_q;

  Register #(.width(32)) PC (.D(multiplexer_1_out), .Q(PC_q), .clk(Clk));  // open: en, clr
  and and_1 (and_1_out, Branch, Zero_Flag);
  RAM #(.addrWidth(24), .dataWidth(32)) ram_1 (.addr(PC_q[23:0]), .data(IR), .clk(Clk), .ld(En));  // open: sel, clr
  Adder #(.width(32)) adder_1 (.a(PC_q), .b(32'h1), .out(adder_1_out));  // open: cin, cout
  Adder #(.width(32)) adder_2 (.a(PC_q), .b(Immediate), .out(adder_2_out));  // open: cin, cout
  Multiplexer #(.width(32), .enable("false")) multiplexer_1 (
    .in0(adder_1_out), .in1(adder_2_out), .out(multiplexer_1_out), .sel(and_1_out));
endmodule

module ALU (
  input  [2:0] ALUOperation,
  input  [31:0] SRC1,
  input  [31:0] SRC2,
  output ZF,
  output [31:0] ALUResult
);

  wire [31:0] adder_1_out, adder_2_out, AND_out, bit_extender_1_out, not_1_out, OR_out;

  assign not_1_out = ~SRC2;  // NOT_Gate not_1, 32 bits wide
  assign AND_out = SRC1 & SRC2;  // AND_Gate AND, 32 bits wide
  assign OR_out = SRC1 | SRC2;  // OR_Gate OR, 32 bits wide
  Adder #(.width(32)) adder_1 (.a(SRC1), .b(SRC2), .out(adder_1_out));  // open: cin, cout
  Adder #(.width(32)) adder_2 (.a(SRC1), .b(not_1_out), .out(adder_2_out), .cin(1'b1));  // open: cout
  assign bit_extender_1_out = {{31{1'b0}}, adder_2_out[31]};  // Bit_Extender bit_extender_1
  Multiplexer #(.select(3), .width(32), .enable("false")) multiplexer_1 (
    .in0(AND_out), .in1(OR_out), .in2(adder_1_out), .in3(bit_extender_1_out), .in6(adder_2_out),
    .out(ALUResult), .sel(ALUOperation));  // open: in4, in5, in7
  nor nor_1 (ZF, ALUResult[0], ALUResult[1], ALUResult[2], ALUResult[3], ALUResult[4], ALUResult[5], ALUResult[6], ALUResult[7], ALUResult[8], ALUResult[9], ALUResult[10], ALUResult[11], ALUResult[12], ALUResult[13], ALUResult[14], ALUResult[15], ALUResult[16], ALUResult[17], ALUResult[18], ALUResult[19], ALUResult[20], ALUResult[21], ALUResult[22], ALUResult[23], ALUResult[24], ALUResult[25], ALUResult[26], ALUResult[27], ALUResult[28], ALUResult[29], ALUResult[30], ALUResult[31]);
endmodule

module IF_RF_ALU_CIRC (
  input  Write,
  output [4:0] ReadReg1,
  output [4:0] ReadReg2,
  output [31:0] ReadData1,
  output [31:0] IR,
  output ZF,
  output [31:0] ALU_Result,
  output [31:0] ReadData2
);

  wire Clock_out;

  Clock Clock (.out(Clock_out));
  // Instruction_Fetch instruction_fetch_1: pin names not known; wires that end beside it: Clock_out, 1'b1, IR
  RegFile32 regfile32_1 (
    .ReadReg1(IR[19:15]), .ReadReg2(IR[24:20]), .Clk(Clock_out), .Write(Write), .WriteReg(IR[11:7]),
    .WriteData({32{1'b0}}), .ReadData1(ReadData1), .ReadData2(ReadData2));
  ALU alu_1 (.ALUOperation(3'b010), .SRC1(ReadData1), .SRC2(ReadData2), .ZF(ZF), .ALUResult(ALU_Result));

  assign ReadReg1 = IR[19:15];
  assign ReadReg2 = IR[24:20];

  // Notes on the sheet:
  //   WriteData
  //   Enable
  //   ALU Operation
endmodule

// DM
module Data_Memory (
  input  [23:0] Address,
  input  [31:0] Write_Data,
  input  MemRead,
  input  MemWrite,
  input  Clock,
  output [31:0] Read_Data
);

  RAM #(.addrWidth(24), .dataWidth(32), .bus("separate")) ram_1 (
    .addr(Address), .din(Write_Data), .data(Read_Data), .str(MemWrite), .clk(Clock), .ld(MemRead));  // open: sel, clr
endmodule

module IF_RF_ALU_DM_CIRC (
  input  Branch,
  input  Write,
  input  MemRead,
  input  MemToReg,
  input  MemWrite,
  input  ALUSrc,
  output [4:0] ReadReg1,
  output [4:0] ReadReg2,
  output [31:0] ReadData1,
  output [31:0] IR,
  output ZF,
  output [31:0] ReadData2,
  output [31:0] ALU_Result,
  output [31:0] Immediate
);

  wire Clock_out;
  wire [23:0] alu_1_aluresult;
  wire [31:0] data_memory_1_read_data, multiplexer_1_out;
  wire [31:24] alu_1_aluresult_2;

  Clock Clock (.out(Clock_out));
  Instruction_Fetch instruction_fetch_1 (
    .Branch(Branch), .Zero_Flag(ZF), .Immediate(Immediate), .Clk(Clock_out), .En(1'b1), .IR(IR));
  ImmGen immgen_1 (.Instruction(IR), .Immediate(Immediate));
  RegFile32 regfile32_1 (
    .ReadReg1(IR[19:15]), .ReadReg2(IR[24:20]), .Clk(Clock_out), .Write(Write), .WriteReg(IR[11:7]),
    .WriteData(ALU_Result), .ReadData1(ReadData1), .ReadData2(ReadData2));
  Multiplexer #(.width(32), .enable("false")) multiplexer_1 (
    .in0(ReadData2), .in1(Immediate), .out(multiplexer_1_out), .sel(ALUSrc));
  ALU alu_1 (
    .ALUOperation(3'b110), .SRC1(ReadData1), .SRC2(multiplexer_1_out), .ZF(ZF),
    .ALUResult({alu_1_aluresult_2, alu_1_aluresult}));
  Data_Memory data_memory_1 (
    .Address(alu_1_aluresult), .Write_Data(ReadData2), .MemRead(MemRead), .MemWrite(MemWrite),
    .Clock(Clock_out), .Read_Data(data_memory_1_read_data));
  Multiplexer #(.width(32), .enable("false")) multiplexer_2 (
    .in0({alu_1_aluresult_2, alu_1_aluresult}), .in1(data_memory_1_read_data), .out(ALU_Result),
    .sel(MemToReg));

  assign ReadReg1 = IR[19:15];
  assign ReadReg2 = IR[24:20];

  // Notes on the sheet:
  //   Enable
  //   ALU Operation
endmodule

module ImmGen (
  input  [31:0] Instruction,
  output [31:0] Immediate
);

  wire comparator_1_eq, comparator_2_eq, comparator_3_eq;
  wire [2:0] priority_encoder_1_out;
  wire [31:0] bit_extender_1_out, bit_extender_2_out, bit_extender_3_out, bit_extender_4_out,
       bit_extender_5_out, bit_extender_6_out, multiplexer_1_out, multiplexer_2_out, multiplexer_3_out;

  Comparator #(.width(7)) comparator_1 (.a(Instruction[6:0]), .b(7'b0000011), .eq(comparator_1_eq));  // open: gt, lt
  Comparator #(.width(7)) comparator_2 (.a(Instruction[6:0]), .b(7'b0100011), .eq(comparator_2_eq));  // open: gt, lt
  Comparator #(.width(7)) comparator_3 (.a(Instruction[6:0]), .b(7'b1100011), .eq(comparator_3_eq));  // open: gt, lt
  Priority_Encoder priority_encoder_1 (
    .in0(comparator_1_eq), .in1(comparator_2_eq), .in2(comparator_3_eq), .out(priority_encoder_1_out),
    .en_in(1'b1));  // open: in3, in4, in5, in6, in7, gs, en_out
  assign bit_extender_1_out = {{20{1'b0}}, Instruction[31:20]};  // Bit_Extender bit_extender_1
  assign bit_extender_2_out = {{20{1'b1}}, Instruction[31:20]};  // Bit_Extender bit_extender_2
  assign bit_extender_3_out = {{20{1'b0}}, {Instruction[31:25], Instruction[11:7]}};  // Bit_Extender bit_extender_3
  assign bit_extender_4_out = {{20{1'b1}}, {Instruction[31:25], Instruction[11:7]}};  // Bit_Extender bit_extender_4
  assign bit_extender_5_out = {{19{1'b0}}, {Instruction[31], Instruction[7], Instruction[30:25], Instruction[11:8], 1'b0}};  // Bit_Extender bit_extender_5
  assign bit_extender_6_out = {{19{1'b1}}, {Instruction[31], Instruction[7], Instruction[30:25], Instruction[11:8], 1'b0}};  // Bit_Extender bit_extender_6
  Multiplexer #(.width(32), .enable("false")) multiplexer_1 (
    .in0(bit_extender_1_out), .in1(bit_extender_2_out), .out(multiplexer_1_out), .sel(Instruction[31]));
  Multiplexer #(.width(32), .enable("false")) multiplexer_2 (
    .in0(bit_extender_3_out), .in1(bit_extender_4_out), .out(multiplexer_2_out), .sel(Instruction[31]));
  Multiplexer #(.width(32), .enable("false")) multiplexer_3 (
    .in0(bit_extender_5_out), .in1(bit_extender_6_out), .out(multiplexer_3_out), .sel(Instruction[31]));
  Multiplexer #(.select(3), .width(32), .enable("false")) multiplexer_4 (
    .in0(multiplexer_1_out), .in1(multiplexer_2_out), .in2(multiplexer_3_out), .out(Immediate),
    .sel(priority_encoder_1_out));  // open: in3, in4, in5, in6, in7
endmodule
