// Logisim project lab_9.circ as structural Verilog: 3 circuits, main circuit main
module main (
  output [15:0] ReadData1,
  output [15:0] ReadData2
);

  wire clock_1_out, clock_2_out;

  Clock clock_1 (.out(clock_1_out));
  Clock clock_2 (.out(clock_2_out));
  write_port_8_16bit_reg write_port_8_16bit_reg_1 (
    .write(1'b1), .clock(clock_1_out), .WriteRegister(3'b011), .WriteData(16'h1f));
  Read_Write_Ports read_write_ports_1 (
    .ReadReg1(3'b000), .ReadReg2(3'b100), .write(1'b1), .clock(clock_2_out), .WriteRegister(3'b100),
    .WriteData(16'h2145), .ReadData1(ReadData1), .ReadData2(ReadData2));

  // Notes on the sheet:
  //   WriteData
  //   Clock
  //   WrtieReg
  //   Write
  //   ReadReg1
  //   ReadReg2
  //   Write
  //   Clock
  //   WrtieReg
  //   WriteData
endmodule

module write_port_8_16bit_reg (
  input  write,
  input  clock,
  input  [2:0] WriteRegister,
  input  [15:0] WriteData
);

  wire and_1_out, and_2_out, and_3_out, and_4_out, and_5_out, and_6_out, and_7_out, and_8_out,
       decoder_1_out0, decoder_1_out1, decoder_1_out2, decoder_1_out3, decoder_1_out4, decoder_1_out5,
       decoder_1_out6, decoder_1_out7;

  Decoder #(.select(3), .enable("false")) decoder_1 (
    .out0(decoder_1_out0), .out1(decoder_1_out1), .out2(decoder_1_out2), .out3(decoder_1_out3),
    .out4(decoder_1_out4), .out5(decoder_1_out5), .out6(decoder_1_out6), .out7(decoder_1_out7),
    .sel(WriteRegister));
  and and_1 (and_1_out, write, decoder_1_out0);
  and and_2 (and_2_out, write, decoder_1_out1);
  and and_3 (and_3_out, write, decoder_1_out2);
  and and_4 (and_4_out, write, decoder_1_out3);
  and and_5 (and_5_out, write, decoder_1_out4);
  and and_6 (and_6_out, write, decoder_1_out5);
  and and_7 (and_7_out, write, decoder_1_out6);
  and and_8 (and_8_out, write, decoder_1_out7);
  Register #(.width(16)) _0 (.D(WriteData), .en(and_1_out), .clk(clock));  // open: Q, clr
  Register #(.width(16)) _1 (.D(WriteData), .en(and_2_out), .clk(clock));  // open: Q, clr
  Register #(.width(16)) _2 (.D(WriteData), .en(and_3_out), .clk(clock));  // open: Q, clr
  Register #(.width(16)) _3 (.D(WriteData), .en(and_4_out), .clk(clock));  // open: Q, clr
  Register #(.width(16)) _4 (.D(WriteData), .en(and_5_out), .clk(clock));  // open: Q, clr
  Register #(.width(16)) _5 (.D(WriteData), .en(and_6_out), .clk(clock));  // open: Q, clr
  Register #(.width(16)) _6 (.D(WriteData), .en(and_7_out), .clk(clock));  // open: Q, clr
  Register #(.width(16)) _7 (.D(WriteData), .en(and_8_out), .clk(clock));  // open: Q, clr
endmodule

module Read_Write_Ports (
  input  [2:0] ReadReg1,
  input  [2:0] ReadReg2,
  input  write,
  input  clock,
  input  [2:0] WriteRegister,
  input  [15:0] WriteData,
  output [15:0] ReadData1,
  output [15:0] ReadData2
);

  wire and_1_out, and_2_out, and_3_out, and_4_out, and_5_out, and_6_out, and_7_out, and_8_out,
       decoder_1_out0, decoder_1_out1, decoder_1_out2, decoder_1_out3, decoder_1_out4, decoder_1_out5,
       decoder_1_out6, decoder_1_out7;
  wire [15:0] _0_q, _1_q, _2_q, _3_q, _4_q, _5_q, _6_q, _7_q;

  Decoder #(.select(3), .enable("false")) decoder_1 (
    .out0(decoder_1_out0), .out1(decoder_1_out1), .out2(decoder_1_out2), .out3(decoder_1_out3),
    .out4(decoder_1_out4), .out5(decoder_1_out5), .out6(decoder_1_out6), .out7(decoder_1_out7),
    .sel(WriteRegister));
  and and_1 (and_1_out, write, decoder_1_out0);
  and and_2 (and_2_out, write, decoder_1_out1);
  and and_3 (and_3_out, write, decoder_1_out2);
  and and_4 (and_4_out, write, decoder_1_out3);
  and and_5 (and_5_out, write, decoder_1_out4);
  and and_6 (and_6_out, write, decoder_1_out5);
  and and_7 (and_7_out, write, decoder_1_out6);
  and and_8 (and_8_out, write, decoder_1_out7);
  Register #(.width(16)) _0 (.D(WriteData), .en(and_1_out), .Q(_0_q), .clk(clock));  // open: clr
  Register #(.width(16)) _1 (.D(WriteData), .en(and_2_out), .Q(_1_q), .clk(clock));  // open: clr
  Register #(.width(16)) _2 (.D(WriteData), .en(and_3_out), .Q(_2_q), .clk(clock));  // open: clr
  Register #(.width(16)) _3 (.D(WriteData), .en(and_4_out), .Q(_3_q), .clk(clock));  // open: clr
  Register #(.width(16)) _4 (.D(WriteData), .en(and_5_out), .Q(_4_q), .clk(clock));  // open: clr
  Register #(.width(16)) _5 (.D(WriteData), .en(and_6_out), .Q(_5_q), .clk(clock));  // open: clr
  Register #(.width(16)) _6 (.D(WriteData), .en(and_7_out), .Q(_6_q), .clk(clock));  // open: clr
  Register #(.width(16)) _7 (.D(WriteData), .en(and_8_out), .Q(_7_q), .clk(clock));  // open: clr
  Multiplexer #(.select(3), .width(16), .enable("false")) multiplexer_1 (
    .in0(_0_q), .in1(_1_q), .in2(_2_q), .in3(_3_q), .in4(_4_q), .in5(_5_q), .in6(_6_q), .in7(_7_q),
    .out(ReadData1), .sel(ReadReg1));
  Multiplexer #(.select(3), .width(16), .enable("false")) multiplexer_2 (
    .in0(_0_q), .in1(_1_q), .in2(_2_q), .in3(_3_q), .in4(_4_q), .in5(_5_q), .in6(_6_q), .in7(_7_q),
    .out(ReadData2), .sel(ReadReg2));
endmodule
