// Logisim project Practicing_RISCV.circ as structural Verilog: 3 circuits, main circuit main
module main (
  input  [3:0] A,
  input  [3:0] B,
  input  [2:0] ALUControl,
  output [3:0] out_4,
  output [3:0] out_5,
  output [3:0] out_6,
  output [3:0] out_7,
  output [3:0] out_8
);

  wire [3:0] multiplexer_1_out, not_1_out;

  assign not_1_out = ~B;  // NOT_Gate not_1, 4 bits wide
  Multiplexer #(.width(4)) multiplexer_1 (.in0(B), .in1(not_1_out), .out(multiplexer_1_out), .sel(ALUControl[0]));
  Adder #(.width(4)) adder_1 (.a(A), .b(multiplexer_1_out), .out(out_4), .cin(ALUControl[0]));  // open: cout
  assign out_5 = A & B;  // AND_Gate and_1, 4 bits wide
  assign out_7 = A | B;  // OR_Gate or_1, 4 bits wide
  assign out_8 = A ^ B;  // XOR_Gate xor_1, 4 bits wide
  Multiplexer #(.select(3), .width(4)) multiplexer_2 (
    .in0(out_4), .in1(out_4), .in2(out_5), .in3(out_7), .in4(out_8), .out(out_6), .sel(ALUControl));  // open: in5, in6, in7
endmodule

module Memory_Learning (
  input  [7:0] in_1,
  input  [7:0] in_2,
  input  in_3,
  input  in_4,
  input  [3:0] in_5,
  input  in_6,
  input  in_7,
  output [7:0] out_8,
  output [7:0] out_9,
  output [3:0] out_10
);

  wire clock_1_out, clock_2_out;

  ROM rom_1 (.addr(in_1), .data(out_8));
  RAM #(.addrWidth(4), .dataWidth(4)) ram_1 (
    .addr(in_5), .we(in_6), .oe(in_7), .clk(clock_1_out), .dout(out_10));  // open: din
  Clock clock_1 (.out(clock_1_out));
  Clock clock_2 (.out(clock_2_out));
  RAM ram_2 (.addr(in_2), .we(in_4), .oe(in_3), .clk(clock_2_out), .dout(out_9));  // open: din

  // Notes on the sheet:
  //   contents of rom_1 (hex, n*v repeats v):
  //   1 23 3 4 5 6
endmodule

module Memory_Addressing (
  input  [3:0] in_1,
  input  in_2,
  input  in_3,
  input  in_4,
  output [3:0] out_5,
  output [3:0] out_6,
  output [3:0] out_7
);

  wire clock_1_out;

  Clock clock_1 (.out(clock_1_out));
  RAM #(.addrWidth(4), .dataWidth(4)) ram_1 (
    .addr(in_1), .we(in_2), .oe(in_3), .clk(clock_1_out), .dout(out_5));  // open: din
  ROM #(.addrWidth(4), .dataWidth(4)) rom_1 (.addr(in_1), .data(out_7));
  Multiplexer #(.width(4)) multiplexer_1 (.in0(out_5), .in1(out_7), .out(out_6), .sel(in_4));

  // Notes on the sheet:
  //   contents of rom_1 (hex, n*v repeats v):
  //   0 5 8
endmodule
